// Logisim project AOC 16a.circ as structural Verilog: 2 circuits, main circuit main
module main (
  input  Sinc,
  input  in_2,
  input  in_3,
  input  in_4,
  input  in_5
);

  wire and_1_out, and_2_out, and_3_out, and_4_out, Clock_out, d_ff_1_q, d_ff_2_q, d_ff_3_q, d_ff_4_q,
       d_ff_5_q, d_ff_6_q, d_ff_7_q, d_ff_8_q, d_ff_9_q, d_ff_10_q, d_ff_11_q, d_ff_12_q, d_ff_13_q,
       d_ff_14_q, d_ff_15_q, d_ff_16_q, display_1_s, display_1_u, display_1_v, display_1_w, display_1_x,
       display_1_y, display_1_z, display_2_s, display_2_u, display_2_v, display_2_w, display_2_x,
       display_2_y, display_2_z, or_1_out;

  Clock Clock (.out(Clock_out));
  D_Flip_Flop d_ff_1 (.clk(Clock_out), .D(d_ff_4_q), .Q(d_ff_1_q), .preset(Sinc));  // open: Qn, en, reset
  _7_Segment_Display u_7_segment_display_1 (
    .g(display_1_s), .f(display_1_w), .a(display_1_x), .b(display_1_y), .e(display_1_v), .d(display_1_u),
    .c(display_1_z));  // open: dp
  D_Flip_Flop d_ff_2 (.clk(Clock_out), .D(d_ff_1_q), .Q(d_ff_2_q), .reset(Sinc));  // open: Qn, preset, en
  and and_1 (and_1_out, d_ff_1_q, in_2);
  Display display_1 (
    .A(in_2), .B(in_3), .C(in_4), .D(in_5), .x(display_1_x), .y(display_1_y), .z(display_1_z),
    .u(display_1_u), .v(display_1_v), .w(display_1_w), .s(display_1_s));
  D_Flip_Flop d_ff_3 (.clk(Clock_out), .D(d_ff_2_q), .Q(d_ff_3_q), .reset(Sinc));  // open: Qn, preset, en
  and and_2 (and_2_out, d_ff_2_q, in_3);
  D_Flip_Flop d_ff_4 (.clk(Clock_out), .D(d_ff_3_q), .Q(d_ff_4_q), .reset(Sinc));  // open: Qn, preset, en
  and and_3 (and_3_out, d_ff_3_q, in_4);
  and and_4 (and_4_out, d_ff_4_q, in_5);
  or or_1 (or_1_out, and_1_out, and_2_out, and_3_out, and_4_out);
  D_Flip_Flop d_ff_5 (.clk(Clock_out), .D(d_ff_14_q), .Q(d_ff_5_q), .preset(Sinc));  // open: Qn, en, reset
  D_Flip_Flop d_ff_6 (.clk(Clock_out), .D(or_1_out), .Q(d_ff_6_q));  // open: Qn, preset, en, reset
  D_Flip_Flop d_ff_7 (.clk(d_ff_5_q), .D(d_ff_6_q), .Q(d_ff_7_q));  // open: Qn, preset, en, reset
  _7_Segment_Display u_7_segment_display_2 (
    .g(display_2_s), .f(display_2_w), .a(display_2_y), .b(display_2_x), .e(display_2_v), .d(display_2_u),
    .c(display_2_z));  // open: dp
  D_Flip_Flop d_ff_8 (.clk(Clock_out), .D(d_ff_5_q), .Q(d_ff_8_q), .reset(Sinc));  // open: Qn, preset, en
  D_Flip_Flop d_ff_9 (.clk(Clock_out), .D(d_ff_6_q), .Q(d_ff_9_q));  // open: Qn, preset, en, reset
  D_Flip_Flop d_ff_10 (.clk(d_ff_5_q), .D(d_ff_9_q), .Q(d_ff_10_q));  // open: Qn, preset, en, reset
  Display display_2 (
    .A(d_ff_16_q), .B(d_ff_13_q), .C(d_ff_10_q), .D(d_ff_7_q), .x(display_2_x), .y(display_2_y),
    .z(display_2_z), .u(display_2_u), .v(display_2_v), .w(display_2_w), .s(display_2_s));
  D_Flip_Flop d_ff_11 (.clk(Clock_out), .D(d_ff_8_q), .Q(d_ff_11_q), .reset(Sinc));  // open: Qn, preset, en
  D_Flip_Flop d_ff_12 (.clk(Clock_out), .D(d_ff_9_q), .Q(d_ff_12_q));  // open: Qn, preset, en, reset
  D_Flip_Flop d_ff_13 (.clk(d_ff_5_q), .D(d_ff_12_q), .Q(d_ff_13_q));  // open: Qn, preset, en, reset
  D_Flip_Flop d_ff_14 (.clk(Clock_out), .D(d_ff_11_q), .Q(d_ff_14_q), .reset(Sinc));  // open: Qn, preset, en
  D_Flip_Flop d_ff_15 (.clk(Clock_out), .D(d_ff_12_q), .Q(d_ff_15_q));  // open: Qn, preset, en, reset
  D_Flip_Flop d_ff_16 (.clk(d_ff_5_q), .D(d_ff_15_q), .Q(d_ff_16_q));  // open: Qn, preset, en, reset
endmodule

module Display (
  input  A,
  input  B,
  input  C,
  input  D,
  output x,
  output y,
  output z,
  output u,
  output v,
  output w,
  output s
);

  wire and_1_out, and_2_out, and_3_out, and_4_out, and_5_out, and_6_out, and_7_out, and_8_out, and_9_out,
       and_10_out, and_11_out, and_12_out, and_13_out, and_14_out, and_15_out, and_16_out, and_17_out,
       and_18_out, and_19_out, and_20_out, and_21_out, and_22_out, and_23_out, and_24_out, and_25_out,
       and_26_out, and_27_out, and_28_out, and_29_out, and_30_out, and_31_out, and_32_out, and_33_out,
       and_34_out, and_35_out, not_1_out, not_2_out, not_3_out, not_4_out, not_5_out, not_6_out, not_7_out,
       not_8_out, not_9_out, not_10_out, not_11_out, not_12_out, not_13_out, not_14_out, not_15_out,
       not_16_out, not_17_out, not_18_out, not_19_out, not_20_out, not_21_out, not_22_out, not_23_out,
       not_24_out, not_25_out, not_26_out, not_27_out, not_28_out, not_29_out, not_30_out, not_31_out,
       not_32_out, not_33_out, not_34_out, not_35_out, not_36_out, not_37_out, not_38_out, not_39_out,
       not_40_out, not_41_out, not_42_out, not_43_out;

  not not_1 (not_1_out, B);
  and and_1 (and_1_out, not_1_out, not_2_out);
  not not_2 (not_2_out, D);
  not not_3 (not_3_out, A);
  and and_2 (and_2_out, not_3_out, C);
  not not_4 (not_4_out, A);
  and and_3 (and_3_out, not_4_out, B, D);
  and and_4 (and_4_out, B, C);
  and and_5 (and_5_out, A, not_5_out, not_6_out);
  not not_5 (not_5_out, B);
  not not_6 (not_6_out, C);
  and and_6 (and_6_out, A, not_7_out);
  not not_7 (not_7_out, D);
  not not_8 (not_8_out, A);
  and and_7 (and_7_out, not_8_out, not_9_out);
  not not_9 (not_9_out, B);
  not not_10 (not_10_out, A);
  and and_8 (and_8_out, not_10_out, not_11_out, not_12_out);
  not not_11 (not_11_out, C);
  not not_12 (not_12_out, D);
  not not_13 (not_13_out, B);
  and and_9 (and_9_out, not_13_out, not_14_out);
  not not_14 (not_14_out, D);
  not not_15 (not_15_out, A);
  and and_10 (and_10_out, not_15_out, C, D);
  and and_11 (and_11_out, A, not_16_out, D);
  not not_16 (not_16_out, C);
  not not_17 (not_17_out, A);
  and and_12 (and_12_out, not_17_out, not_18_out);
  not not_18 (not_18_out, C);
  not not_19 (not_19_out, A);
  and and_13 (and_13_out, not_19_out, D);
  not not_20 (not_20_out, C);
  and and_14 (and_14_out, not_20_out, D);
  not not_21 (not_21_out, A);
  and and_15 (and_15_out, not_21_out, B);
  and and_16 (and_16_out, A, not_22_out);
  not not_22 (not_22_out, B);
  not not_23 (not_23_out, A);
  and and_17 (and_17_out, not_23_out, not_24_out, not_25_out);
  not not_24 (not_24_out, B);
  not not_25 (not_25_out, D);
  not not_26 (not_26_out, B);
  and and_18 (and_18_out, not_26_out, C, D);
  and and_19 (and_19_out, B, not_27_out, D);
  not not_27 (not_27_out, C);
  and and_20 (and_20_out, B, C, not_28_out);
  not not_28 (not_28_out, D);
  and and_21 (and_21_out, A, not_29_out);
  not not_29 (not_29_out, C);
  not not_30 (not_30_out, B);
  and and_22 (and_22_out, not_30_out, not_31_out);
  not not_31 (not_31_out, D);
  and and_23 (and_23_out, C, not_32_out);
  not not_32 (not_32_out, D);
  and and_24 (and_24_out, A, C);
  and and_25 (and_25_out, A, B);
  not not_33 (not_33_out, C);
  and and_26 (and_26_out, not_33_out, not_34_out);
  not not_34 (not_34_out, D);
  not not_35 (not_35_out, A);
  and and_27 (and_27_out, not_35_out, B, not_36_out);
  not not_36 (not_36_out, C);
  and and_28 (and_28_out, B, not_37_out);
  not not_37 (not_37_out, D);
  and and_29 (and_29_out, A, not_38_out);
  not not_38 (not_38_out, B);
  and and_30 (and_30_out, A, C);
  not not_39 (not_39_out, B);
  and and_31 (and_31_out, not_39_out, C);
  and and_32 (and_32_out, C, not_40_out);
  not not_40 (not_40_out, D);
  not not_41 (not_41_out, A);
  and and_33 (and_33_out, not_41_out, B, not_42_out);
  not not_42 (not_42_out, C);
  and and_34 (and_34_out, A, not_43_out);
  not not_43 (not_43_out, B);
  and and_35 (and_35_out, A, D);
  or or_1 (y, and_7_out, and_8_out, and_9_out, and_10_out, and_11_out);
  or or_2 (z, and_12_out, and_13_out, and_14_out, and_15_out, and_16_out);
  or or_3 (u, and_17_out, and_18_out, and_19_out, and_20_out, and_21_out);
  or or_4 (v, and_22_out, and_23_out, and_24_out, and_25_out);
  or or_5 (w, and_26_out, and_27_out, and_28_out, and_29_out, and_30_out);
  or or_6 (s, and_31_out, and_32_out, and_33_out, and_34_out, and_35_out);
  or or_7 (x, and_1_out, and_2_out, and_3_out, and_4_out, and_5_out, and_6_out);
endmodule
