// Logisim project AOC 22.circ as structural Verilog: 4 circuits, main circuit main
module main (
  input  in_1,
  input  in_2,
  input  in_3,
  input  in_4,
  input  in_5,
  input  in_6,
  input  in_7,
  input  in_8,
  input  in_9,
  input  in_10,
  input  in_11,
  input  in_12,
  input  in_13,
  input  in_14,
  input  in_15,
  input  in_16,
  input  in_17,
  input  in_18,
  input  in_19,
  input  in_20,
  output out_21,
  output out_22,
  output out_23,
  output out_24
);

  wire and_1_out, and_2_out, and_3_out, and_4_out, and_5_out, and_6_out, and_7_out, and_8_out, and_9_out,
       and_10_out, and_11_out, and_12_out, and_13_out, and_14_out, and_15_out, and_16_out, and_17_out,
       and_18_out, and_19_out, and_20_out, and_21_out, and_22_out, and_23_out, and_24_out, and_25_out,
       and_26_out, and_27_out, and_28_out, and_29_out, and_30_out, and_31_out, and_35_out, clock_1_out,
       d_ff_1_q, d_ff_2_q, d_ff_3_q, d_ff_4_q, display_1_s, display_1_u, display_1_v, display_1_w,
       display_1_x, display_1_y, display_1_z, display_2_s, display_2_u, display_2_v, display_2_w,
       display_2_x, display_2_y, display_2_z, display_3_s, display_3_u, display_3_v, display_3_w,
       display_3_x, display_3_y, display_3_z, multi_1_a, multi_1_b, multi_1_c, multi_1_d, or_1_out, or_2_out,
       or_3_out, or_4_out, or_5_out, or_6_out, or_7_out, or_8_out, or_9_out, or_10_out, soma_1_a, soma_1_b,
       soma_1_c, soma_1_d, t_ff_1_q, t_ff_2_q, t_ff_2_qn;

  Clock clock_1 (.out(clock_1_out));
  T_Flip_Flop t_ff_1 (.clk(t_ff_2_qn), .T(in_1), .Q(t_ff_1_q));  // open: Qn, preset, reset, en
  and and_1 (and_1_out, ~t_ff_2_q, ~t_ff_1_q);  // AND_Gate
  and and_2 (and_2_out, t_ff_2_q, ~t_ff_1_q);  // AND_Gate
  and and_3 (and_3_out, ~t_ff_2_q, t_ff_1_q);  // AND_Gate
  T_Flip_Flop t_ff_2 (.clk(clock_1_out), .T(in_1), .Q(t_ff_2_q), .Qn(t_ff_2_qn));  // open: preset, reset, en
  and and_4 (and_4_out, and_1_out, in_3);
  and and_5 (and_5_out, and_1_out, in_2);
  and and_6 (and_6_out, and_2_out, in_8);
  and and_7 (and_7_out, and_2_out, in_9);
  and and_8 (and_8_out, and_3_out, in_16);
  and and_9 (and_9_out, and_3_out, in_15);
  buf and_10 (and_10_out, in_4);  // AND_Gate
  and and_11 (and_11_out, and_2_out, in_10);
  and and_12 (and_12_out, and_3_out, in_17);
  and and_13 (and_13_out, and_1_out, in_5);
  and and_14 (and_14_out, and_2_out, in_11);
  and and_15 (and_15_out, and_3_out, in_18);
  and and_16 (and_16_out, and_1_out, in_6);
  and and_17 (and_17_out, and_1_out, in_7);
  and and_18 (and_18_out, and_2_out, in_13);
  and and_19 (and_19_out, and_2_out, in_12);
  and and_20 (and_20_out, and_3_out, in_20);
  and and_21 (and_21_out, and_3_out, in_19);
  or or_1 (or_1_out, and_5_out, and_6_out, and_9_out);
  or or_2 (or_2_out, and_4_out, and_7_out, and_8_out);
  or or_3 (or_3_out, and_10_out, and_11_out, and_12_out);
  or or_4 (or_4_out, and_13_out, and_14_out, and_15_out);
  or or_5 (or_5_out, and_16_out, and_19_out, and_21_out);
  or or_6 (or_6_out, and_17_out, and_18_out, and_20_out);
  Display display_1 (
    .A(in_14), .B(in_14), .C(or_3_out), .D(or_4_out), .x(display_1_x), .y(display_1_y), .z(display_1_z),
    .u(display_1_u), .v(display_1_v), .w(display_1_w), .s(display_1_s));
  _7_Segment_Display u_7_segment_display_1 (
    .g(display_1_s), .f(display_1_w), .a(display_1_x), .b(display_1_y), .e(display_1_v), .d(display_1_u),
    .c(display_1_z));  // open: dp
  Display display_2 (
    .A(in_14), .B(in_14), .C(or_1_out), .D(or_2_out), .x(display_2_x), .y(display_2_y), .z(display_2_z),
    .u(display_2_u), .v(display_2_v), .w(display_2_w), .s(display_2_s));
  _7_Segment_Display u_7_segment_display_2 (
    .g(display_2_s), .f(display_2_w), .a(display_2_x), .b(display_2_y), .e(display_2_v), .d(display_2_u),
    .c(display_2_z));  // open: dp
  and and_22 (and_22_out, or_5_out, ~or_6_out);  // AND_Gate
  and and_23 (and_23_out, or_4_out, and_22_out);
  and and_24 (and_24_out, or_3_out, and_22_out);
  and and_25 (and_25_out, or_2_out, and_22_out);
  and and_26 (and_26_out, or_1_out, and_22_out);
  Soma soma_1 (
    .a1(and_24_out), .a2(and_23_out), .b1(and_26_out), .b2(and_25_out), .a(soma_1_a), .b(soma_1_b),
    .c(soma_1_c), .d(soma_1_d));
  or or_7 (or_7_out, soma_1_a, multi_1_a);
  or or_8 (or_8_out, soma_1_b, multi_1_b);
  or or_9 (or_9_out, soma_1_c, multi_1_c);
  and and_27 (and_27_out, ~or_5_out, or_6_out);  // AND_Gate
  and and_28 (and_28_out, or_3_out, and_27_out);
  and and_29 (and_29_out, or_4_out, and_27_out);
  Multi multi_1 (
    .a1(and_28_out), .a2(and_29_out), .b1(and_31_out), .b2(and_30_out), .a(multi_1_a), .b(multi_1_b),
    .c(multi_1_c), .d(multi_1_d));
  or or_10 (or_10_out, soma_1_d, multi_1_d);
  Display display_3 (
    .A(or_7_out), .B(or_8_out), .C(or_9_out), .D(or_10_out), .x(display_3_x), .y(display_3_y),
    .z(display_3_z), .u(display_3_u), .v(display_3_v), .w(display_3_w), .s(display_3_s));
  _7_Segment_Display u_7_segment_display_3 (
    .g(display_3_s), .f(display_3_w), .a(display_3_x), .b(display_3_y), .e(display_3_v), .d(display_3_u),
    .c(display_3_z));  // open: dp
  and and_30 (and_30_out, or_2_out, and_27_out);
  and and_31 (and_31_out, or_1_out, and_27_out);
  D_Flip_Flop d_ff_1 (.clk(clock_1_out), .D(or_7_out), .Q(d_ff_1_q));  // open: Qn, preset, en, reset
  and and_32 (out_21, d_ff_1_q, and_35_out);
  D_Flip_Flop d_ff_2 (.clk(clock_1_out), .D(or_8_out), .Q(d_ff_2_q));  // open: Qn, preset, en, reset
  and and_33 (out_22, d_ff_2_q, and_35_out);
  D_Flip_Flop d_ff_3 (.clk(clock_1_out), .D(or_9_out), .Q(d_ff_3_q));  // open: Qn, preset, en, reset
  and and_34 (out_23, d_ff_3_q, and_35_out);
  and and_35 (and_35_out, or_5_out, or_6_out);
  D_Flip_Flop d_ff_4 (.clk(clock_1_out), .D(or_10_out), .Q(d_ff_4_q));  // open: Qn, preset, en, reset
  and and_36 (out_24, d_ff_4_q, and_35_out);
endmodule

module Display (
  input  A,
  input  B,
  input  C,
  input  D,
  output x,
  output y,
  output z,
  output u,
  output v,
  output w,
  output s
);

  wire and_1_out, and_2_out, and_3_out, and_4_out, and_5_out, and_6_out, and_7_out, and_8_out, and_9_out,
       and_10_out, and_11_out, and_12_out, and_13_out, and_14_out, and_15_out, and_16_out, and_17_out,
       and_18_out, and_19_out, and_20_out, and_21_out, and_22_out, and_23_out, and_24_out, and_25_out,
       and_26_out, and_27_out, and_28_out, and_29_out, and_30_out, and_31_out, and_32_out, and_33_out,
       and_34_out, and_35_out, not_1_out, not_2_out, not_3_out, not_4_out, not_5_out, not_6_out, not_7_out,
       not_8_out, not_9_out, not_10_out, not_11_out, not_12_out, not_13_out, not_14_out, not_15_out,
       not_16_out, not_17_out, not_18_out, not_19_out, not_20_out, not_21_out, not_22_out, not_23_out,
       not_24_out, not_25_out, not_26_out, not_27_out, not_28_out, not_29_out, not_30_out, not_31_out,
       not_32_out, not_33_out, not_34_out, not_35_out, not_36_out, not_37_out, not_38_out, not_39_out,
       not_40_out, not_41_out, not_42_out, not_43_out;

  not not_1 (not_1_out, B);
  and and_1 (and_1_out, not_1_out, not_2_out);
  not not_2 (not_2_out, D);
  not not_3 (not_3_out, A);
  and and_2 (and_2_out, not_3_out, C);
  not not_4 (not_4_out, A);
  and and_3 (and_3_out, not_4_out, B, D);
  and and_4 (and_4_out, B, C);
  not not_5 (not_5_out, B);
  and and_5 (and_5_out, A, not_5_out, not_6_out);
  not not_6 (not_6_out, C);
  and and_6 (and_6_out, A, not_7_out);
  not not_7 (not_7_out, D);
  not not_8 (not_8_out, A);
  and and_7 (and_7_out, not_8_out, not_9_out);
  not not_9 (not_9_out, B);
  not not_10 (not_10_out, A);
  not not_11 (not_11_out, C);
  and and_8 (and_8_out, not_10_out, not_11_out, not_12_out);
  not not_12 (not_12_out, D);
  not not_13 (not_13_out, B);
  and and_9 (and_9_out, not_13_out, not_14_out);
  not not_14 (not_14_out, D);
  not not_15 (not_15_out, A);
  and and_10 (and_10_out, not_15_out, C, D);
  not not_16 (not_16_out, C);
  and and_11 (and_11_out, A, not_16_out, D);
  not not_17 (not_17_out, A);
  and and_12 (and_12_out, not_17_out, not_18_out);
  not not_18 (not_18_out, C);
  not not_19 (not_19_out, A);
  and and_13 (and_13_out, not_19_out, D);
  not not_20 (not_20_out, C);
  and and_14 (and_14_out, not_20_out, D);
  not not_21 (not_21_out, A);
  and and_15 (and_15_out, not_21_out, B);
  and and_16 (and_16_out, A, not_22_out);
  not not_22 (not_22_out, B);
  not not_23 (not_23_out, A);
  and and_17 (and_17_out, not_23_out, not_24_out, not_25_out);
  not not_24 (not_24_out, B);
  not not_25 (not_25_out, D);
  not not_26 (not_26_out, B);
  and and_18 (and_18_out, not_26_out, C, D);
  and and_19 (and_19_out, B, not_27_out, D);
  not not_27 (not_27_out, C);
  and and_20 (and_20_out, B, C, not_28_out);
  not not_28 (not_28_out, D);
  and and_21 (and_21_out, A, not_29_out);
  not not_29 (not_29_out, C);
  not not_30 (not_30_out, B);
  and and_22 (and_22_out, not_30_out, not_31_out);
  not not_31 (not_31_out, D);
  and and_23 (and_23_out, C, not_32_out);
  not not_32 (not_32_out, D);
  and and_24 (and_24_out, A, C);
  and and_25 (and_25_out, A, B);
  not not_33 (not_33_out, C);
  and and_26 (and_26_out, not_33_out, not_34_out);
  not not_34 (not_34_out, D);
  not not_35 (not_35_out, A);
  and and_27 (and_27_out, not_35_out, B, not_36_out);
  not not_36 (not_36_out, C);
  and and_28 (and_28_out, B, not_37_out);
  not not_37 (not_37_out, D);
  and and_29 (and_29_out, A, not_38_out);
  not not_38 (not_38_out, B);
  and and_30 (and_30_out, A, C);
  not not_39 (not_39_out, B);
  and and_31 (and_31_out, not_39_out, C);
  and and_32 (and_32_out, C, not_40_out);
  not not_40 (not_40_out, D);
  not not_41 (not_41_out, A);
  and and_33 (and_33_out, not_41_out, B, not_42_out);
  not not_42 (not_42_out, C);
  and and_34 (and_34_out, A, not_43_out);
  not not_43 (not_43_out, B);
  and and_35 (and_35_out, A, D);
  or or_1 (y, and_7_out, and_8_out, and_9_out, and_10_out, and_11_out);
  or or_2 (z, and_12_out, and_13_out, and_14_out, and_15_out, and_16_out);
  or or_3 (u, and_17_out, and_18_out, and_19_out, and_20_out, and_21_out);
  or or_4 (v, and_22_out, and_23_out, and_24_out, and_25_out);
  or or_5 (w, and_26_out, and_27_out, and_28_out, and_29_out, and_30_out);
  or or_6 (s, and_31_out, and_32_out, and_33_out, and_34_out, and_35_out);
  or or_7 (x, and_1_out, and_2_out, and_3_out, and_4_out, and_5_out, and_6_out);
endmodule

module Soma (
  input  a1,
  input  a2,
  input  b1,
  input  b2,
  output a,
  output b,
  output c,
  output d
);

  wire and_1_out, and_2_out, and_3_out, and_4_out, and_5_out, and_6_out, and_7_out, and_8_out, and_9_out,
       and_10_out, and_11_out, not_1_out, not_2_out, not_3_out, not_4_out, not_5_out, not_6_out, not_7_out,
       not_8_out, not_9_out, not_10_out, not_11_out, not_12_out;

  and and_1 (and_1_out, a2, b1, b2);
  and and_2 (and_2_out, a1, b1);
  and and_3 (and_3_out, a1, a2, b2);
  not not_1 (not_1_out, a1);
  not not_2 (not_2_out, a2);
  not not_3 (not_3_out, a1);
  not not_4 (not_4_out, b2);
  not not_5 (not_5_out, a1);
  not not_6 (not_6_out, b1);
  not not_7 (not_7_out, a2);
  not not_8 (not_8_out, b1);
  not not_9 (not_9_out, b1);
  not not_10 (not_10_out, b2);
  not not_11 (not_11_out, a2);
  and and_4 (and_4_out, not_11_out, b2);
  and and_5 (and_5_out, a2, not_12_out);
  not not_12 (not_12_out, b2);
  or or_1 (b, and_1_out, and_2_out, and_3_out);
  and and_6 (and_6_out, not_1_out, not_2_out, b1);
  and and_7 (and_7_out, not_3_out, b1, not_4_out);
  and and_8 (and_8_out, not_5_out, a2, not_6_out, b2);
  and and_9 (and_9_out, a1, not_7_out, not_8_out);
  and and_10 (and_10_out, a1, not_9_out, not_10_out);
  and and_11 (and_11_out, a1, a2, b1, b2);
  or or_2 (d, and_4_out, and_5_out);
  or or_3 (c, and_6_out, and_7_out, and_8_out, and_9_out, and_10_out, and_11_out);

  assign a = 1'b0;
endmodule

module Multi (
  input  a1,
  input  a2,
  input  b1,
  input  b2,
  output a,
  output b,
  output c,
  output d
);

  wire and_2_out, and_3_out, and_4_out, and_5_out, and_6_out, and_7_out, not_1_out, not_2_out, not_3_out,
       not_4_out, not_5_out, not_6_out;

  and and_1 (a, a1, a2, b1, b2);
  and and_2 (and_2_out, a1, not_1_out, b1);
  not not_1 (not_1_out, a2);
  and and_3 (and_3_out, a1, b1, not_2_out);
  not not_2 (not_2_out, b2);
  not not_3 (not_3_out, a1);
  and and_4 (and_4_out, not_3_out, a2, b1);
  and and_5 (and_5_out, a2, b1, not_4_out);
  not not_4 (not_4_out, b2);
  not not_5 (not_5_out, a2);
  and and_6 (and_6_out, a1, not_5_out, b2);
  not not_6 (not_6_out, b1);
  and and_7 (and_7_out, a1, not_6_out, b2);
  and and_8 (d, a2, b2);
  or or_1 (b, and_2_out, and_3_out);
  or or_2 (c, and_4_out, and_5_out, and_6_out, and_7_out);
endmodule
