// Logisim project AOC 6.circ as structural Verilog: 1 circuit, main circuit main
module main (
  input  A,
  input  B,
  input  D,
  input  C,
  input  A_2,
  input  B_2,
  input  C_2,
  input  D_2,
  input  A_3,
  input  B_3,
  input  C_3,
  input  D_3,
  input  E,
  input  A_4,
  input  B_4,
  input  C_4,
  input  D_4,
  output out_18,
  output out_19,
  output out_20,
  output out_21
);

  wire and_1_out, and_2_out, and_3_out, and_4_out, and_5_out, and_6_out, nand_1_out, nand_2_out, not_1_out,
       not_2_out, or_1_out, or_2_out, or_4_out;

  not not_1 (not_1_out, B);
  not not_2 (not_2_out, C_2);
  and and_1 (and_1_out, A, not_1_out);
  nand nand_1 (nand_1_out, D, C);
  and and_2 (and_2_out, A_2, B_2, not_2_out);
  nand nand_2 (nand_2_out, C_2, D_2);
  and and_3 (and_3_out, A_3, B_3);
  and and_4 (and_4_out, C_3, D_3, E);
  or or_1 (or_1_out, A_4, B_4);
  and and_5 (and_5_out, C_4, D_4);
  nor nor_1 (out_18, and_1_out, nand_1_out);
  or or_2 (or_2_out, and_2_out, nand_2_out);
  or or_3 (out_20, and_3_out, and_4_out);
  or or_4 (or_4_out, B_4, and_5_out);
  nor nor_2 (out_19, or_2_out, D_2);
  and and_6 (and_6_out, or_1_out, or_4_out);
  or or_5 (out_21, A_4, and_6_out);
endmodule
